# Fritzing sketch Mozzi_Lowpass+Notch (saved by Fritzing 0.7.11b)
breadboards: 1

parts:
  R1 = Resistor [tolerance=±1% resistance=680 package=THT]
  R2 = Resistor [tolerance=±1% resistance=680 package=THT]
  C1 = Ceramic Capacitor [capacitance=220nF package="100 mil [THT, multilayer]"]
  C2 = Ceramic Capacitor [capacitance=220nF package="100 mil [THT, multilayer]"]
  C3 = Ceramic Capacitor [capacitance=1nF package="100 mil [THT, multilayer]"]
  R3 = Resistor [tolerance=±5% resistance=330 package=THT]
  R4 = Resistor [tolerance=±5% resistance=270 package=THT]
  C4 = Ceramic Capacitor [capacitance=100nF package="100 mil [THT, multilayer]"]
  TRS1 = Stereo Jack (TRS) 3.5mm [package="PG203J [THT]"]

nets:
  N1: R1.Pin_0, C2.1, R4.Pin_1, C4.0
  N2: R1.Pin_1, R2.Pin_0, C1.1
  N3: R2.Pin_1, C3.0, TRS1.Tip
  GND: C1.0, R3.Pin_1, C4.1, TRS1.Sleeve
  N4: C2.0, C3.1, R3.Pin_0

notes:
  6kHz low-pass and 16384Hz notch filter
  input from arduino
  from arduino pin 9 (for standard arduinos)
  3.5 mm jack audio out
  Parts
  R1,R2: 680Ω
  R3: 330Ω
  R4: 270Ω
  C1,C2: 220nF
  C3: 1nF
  C4: 100nF
  audio out
  R4 and C4 are the
  6k low-pass filter.
  They can be omitted for a
  brighter, noiser sound.
  in
  out
  gnd
